// Logisim project Somador8bits.circ as structural Verilog: 3 circuits, main circuit completo
module completo (
  input  Cin,
  input  a,
  input  b,
  output s,
  output c
);

  wire and_1_out, and_2_out, and_3_out, xor_2_out;

  and and_1 (and_1_out, b, a);
  and and_2 (and_2_out, b, Cin);
  and and_3 (and_3_out, a, Cin);
  xor xor_1 (s, Cin, xor_2_out);
  xor xor_2 (xor_2_out, a, b);
  or or_1 (c, and_1_out, and_2_out, and_3_out);
endmodule

module _4bits (
  input  Cin,
  input  a0,
  input  b0,
  input  a1,
  input  b1,
  input  a2,
  input  b2,
  input  a3,
  input  b3,
  output s0,
  output s1,
  output s2,
  output s3,
  output c
);

  wire completo_1_c, completo_2_c, completo_3_c;

  completo completo_1 (.Cin(Cin), .a(a0), .b(b0), .s(s0), .c(completo_1_c));
  completo completo_2 (.Cin(completo_1_c), .a(a1), .b(b1), .s(s1), .c(completo_2_c));
  completo completo_3 (.Cin(completo_2_c), .a(a2), .b(b2), .s(s2), .c(completo_3_c));
  completo completo_4 (.Cin(completo_3_c), .a(a3), .b(b3), .s(s3), .c(c));
endmodule

module _8bits (
  input  Cin,
  input  a0,
  input  b0,
  input  a1,
  input  b1,
  input  a2,
  input  b2,
  input  a3,
  input  b3,
  input  a4,
  input  b4,
  input  a5,
  input  b5,
  input  a6,
  input  b6,
  input  a7,
  input  b7,
  output out_18,
  output out_19,
  output out_20,
  output out_21,
  output out_22,
  output out_23,
  output out_24,
  output out_25,
  output out_26
);

  wire n4bits_1_c;

  _4bits u_4bits_1 (
    .Cin(Cin), .a0(a0), .b0(b0), .a1(a1), .b1(b1), .a2(a2), .b2(b2), .a3(a3), .b3(b3), .s0(out_18),
    .s1(out_19), .s2(out_20), .s3(out_21), .c(n4bits_1_c));
  _4bits u_4bits_2 (
    .Cin(n4bits_1_c), .a0(a4), .b0(b4), .a1(a5), .b1(b5), .a2(a6), .b2(b6), .a3(a7), .b3(b7), .s0(out_22),
    .s1(out_23), .s2(out_24), .s3(out_25), .c(out_26));
endmodule
