// Logisim project aula_29_05.circ as structural Verilog: 1 circuit, main circuit main
module main (
  input  in_1
);

  wire and_1_out, and_2_out, clock_1_out, clock_2_out, clock_3_out;
  wire [2:0] t_ff_1_q;
  wire [3:0] t_ff_7_q, t_ff_8_q;

  Clock clock_1 (.out(clock_1_out));
  Clock clock_2 (.out(clock_2_out));
  T_Flip_Flop #(.trigger("falling")) t_ff_1 (
    .clk(clock_1_out), .T(1'b1), .Q(t_ff_1_q[0]));  // open: Qn, preset, reset, en
  T_Flip_Flop t_ff_2 (.clk(clock_2_out), .T(1'b1), .Q(t_ff_7_q[3]), .preset(and_1_out));  // open: Qn, reset, en
  and and_1 (and_1_out, ~t_ff_7_q[3], ~t_ff_7_q[2], ~t_ff_7_q[1], t_ff_7_q[0]);  // AND_Gate
  T_Flip_Flop #(.trigger("falling")) t_ff_3 (
    .clk(t_ff_1_q[0]), .T(1'b1), .Q(t_ff_1_q[1]));  // open: Qn, preset, reset, en
  Hex_Digit_Display hex_digit_display_1 (.value({in_1, t_ff_1_q}));  // open: dp
  T_Flip_Flop t_ff_4 (.clk(t_ff_7_q[3]), .T(1'b1), .Q(t_ff_7_q[2]), .reset(and_1_out));  // open: Qn, preset, en
  T_Flip_Flop #(.trigger("falling")) t_ff_5 (
    .clk(t_ff_1_q[1]), .T(1'b1), .Q(t_ff_1_q[2]));  // open: Qn, preset, reset, en
  T_Flip_Flop t_ff_6 (.clk(t_ff_7_q[2]), .T(1'b1), .Q(t_ff_7_q[1]), .reset(and_1_out));  // open: Qn, preset, en
  Clock clock_3 (.out(clock_3_out));
  and and_2 (and_2_out, t_ff_8_q[3], ~t_ff_8_q[2], t_ff_8_q[0], ~t_ff_8_q[1]);  // AND_Gate
  T_Flip_Flop t_ff_7 (.clk(t_ff_7_q[1]), .T(1'b1), .Q(t_ff_7_q[0]), .reset(and_1_out));  // open: Qn, preset, en
  Hex_Digit_Display hex_digit_display_2 (.value(t_ff_7_q));  // open: dp
  T_Flip_Flop #(.trigger("falling")) t_ff_8 (
    .clk(clock_3_out), .T(1'b1), .Q(t_ff_8_q[0]), .preset(and_2_out));  // open: Qn, reset, en
  T_Flip_Flop #(.trigger("falling")) t_ff_9 (
    .clk(t_ff_8_q[0]), .T(1'b1), .Q(t_ff_8_q[1]), .reset(and_2_out));  // open: Qn, preset, en
  Hex_Digit_Display hex_digit_display_3 (.value(t_ff_8_q));  // open: dp
  T_Flip_Flop #(.trigger("falling")) t_ff_10 (
    .clk(t_ff_8_q[1]), .T(1'b1), .Q(t_ff_8_q[2]), .reset(and_2_out));  // open: Qn, preset, en
  T_Flip_Flop #(.trigger("falling")) t_ff_11 (
    .clk(t_ff_8_q[2]), .T(1'b1), .Q(t_ff_8_q[3]), .reset(and_2_out));  // open: Qn, preset, en
endmodule
