// Logisim project circuito01.circ as structural Verilog: 1 circuit, main circuit main
module main (
  input  a,
  input  b,
  input  c,
  input  in_4,
  input  in_5,
  input  in_6,
  input  in_7,
  input  in_8,
  input  in_9,
  input  in_10,
  input  in_11,
  output out_12,
  output out_13,
  output out_14,
  output out_15,
  output out_16
);

  wire and_1_out, and_2_out, and_3_out, and_4_out, and_5_out, and_6_out, and_7_out, and_8_out, and_9_out,
       not_1_out, not_2_out, not_5_out, or_1_out;

  and and_1 (and_1_out, in_10, in_11);
  and and_2 (and_2_out, in_10, in_11);
  or or_1 (or_1_out, a, b);
  not not_1 (not_1_out, in_5);
  and and_3 (and_3_out, not_1_out, in_7);
  and and_4 (and_4_out, in_5, not_2_out);
  not not_2 (not_2_out, in_7);
  or or_2 (out_15, and_1_out, and_2_out);
  and and_5 (and_5_out, or_1_out, c);
  // AND_Gate and_6 has open pins: out=and_6_out
  // NAND_Gate nand_1 is placed but not wired
  or or_3 (out_14, and_3_out, and_4_out);
  not not_3 (out_12, and_5_out);
  // NOT_Gate not_4 has open pins: in=and_6_out, out=open
  // XOR_Gate xor_1 is placed but not wired
  // NOR_Gate nor_1 is placed but not wired
  not not_5 (not_5_out, in_4);
  buf and_7 (and_7_out, in_6);  // AND_Gate
  and and_8 (and_8_out, in_8, in_9);
  or or_4 (out_16, and_8_out, and_9_out);
  and and_9 (and_9_out, in_8, in_9);
  or or_5 (out_13, not_5_out, and_7_out);
endmodule
