// Logisim project sequencias.circ as structural Verilog: 1 circuit, main circuit main
module main (
);

  wire and_1_out, and_2_out, clock_1_out, clock_2_out, clock_3_out, or_1_out, or_2_out, q0_2_qn, q1_2_qn,
       q2_2_qn;
  wire [2:0] q0_q;
  wire [3:0] j_k_ff_4_q, q0_2_q;

  Clock clock_1 (.out(clock_1_out));
  and and_1 (and_1_out, q2_2_qn, q1_2_qn);
  Clock clock_2 (.out(clock_2_out));
  J_K_Flip_Flop q3 (.J(and_1_out), .clk(clock_1_out), .K(q0_2_q[2]), .Q(q0_2_q[3]));  // open: Qn, preset, en, reset
  J_K_Flip_Flop q2 (.J(q0_q[0]), .clk(clock_2_out), .K(q0_q[0]), .Q(q0_q[2]));  // open: Qn, preset, en, reset
  or or_1 (or_1_out, q0_2_q[3], q0_2_qn);
  or or_2 (or_2_out, q0_2_q[3], q0_2_q[1]);
  Hex_Digit_Display hex_digit_display_1 (.value(q0_2_q));  // open: dp
  J_K_Flip_Flop q1 (.J(1'b1), .clk(clock_2_out), .K(1'b1), .Q(q0_q[1]));  // open: Qn, preset, en, reset
  Hex_Digit_Display hex_digit_display_2 (.value({1'b0, q0_q}));  // open: dp
  J_K_Flip_Flop q2_2 (
    .J(or_1_out), .clk(clock_1_out), .K(or_2_out), .Q(q0_2_q[2]), .Qn(q2_2_qn));  // open: preset, en, reset
  J_K_Flip_Flop q0 (.J(1'b1), .clk(clock_2_out), .K(1'b1), .Q(q0_q[0]));  // open: Qn, preset, en, reset
  J_K_Flip_Flop q1_2 (
    .J(1'b1), .clk(clock_1_out), .K(q2_2_qn), .Q(q0_2_q[1]), .Qn(q1_2_qn));  // open: preset, en, reset
  and and_2 (and_2_out, q0_2_q[3], q1_2_qn);
  J_K_Flip_Flop q0_2 (
    .J(1'b1), .clk(clock_1_out), .K(and_2_out), .Q(q0_2_q[0]), .Qn(q0_2_qn));  // open: preset, en, reset
  Clock clock_3 (.out(clock_3_out));
  J_K_Flip_Flop j_k_ff_1 (
    .J(j_k_ff_4_q[2]), .clk(clock_3_out), .K(1'b1), .Q(j_k_ff_4_q[3]));  // open: Qn, preset, en, reset
  Hex_Digit_Display hex_digit_display_3 (.value(j_k_ff_4_q));  // open: dp
  J_K_Flip_Flop j_k_ff_2 (
    .J(j_k_ff_4_q[1]), .clk(clock_3_out), .K(1'b1), .Q(j_k_ff_4_q[2]));  // open: Qn, preset, en, reset
  J_K_Flip_Flop j_k_ff_3 (
    .J(j_k_ff_4_q[0]), .clk(clock_3_out), .K(1'b1), .Q(j_k_ff_4_q[1]));  // open: Qn, preset, en, reset
  J_K_Flip_Flop j_k_ff_4 (
    .J(j_k_ff_4_q[3]), .clk(clock_3_out), .K(1'b1), .Q(j_k_ff_4_q[0]));  // open: Qn, preset, en, reset
endmodule
