// Logisim project trabalho.circ as structural Verilog
module meioSomaPG (
  input  a,
  input  b,
  output p,
  output g
);

  or or_1 (p, a, b);
  and and_1 (g, a, b);
endmodule

module CL4bits (
  input  c0,
  input  b0,
  input  a0,
  input  b1,
  input  a1,
  input  b2,
  input  a2,
  input  b3,
  input  a3,
  output s0,
  output s1,
  output s2,
  output s3,
  output c4
);

  wire _0_g, _0_p, _1_g, _1_p, _2_g, _2_p, _3_g, _3_p, and_1_out, and_2_out, and_3_out, and_4_out, and_5_out,
       and_6_out, and_7_out, and_8_out, and_9_out, and_10_out, or_2_out, or_3_out;

  meioSomaPG _0 (.a(a0), .b(b0), .p(_0_p), .g(_0_g));
  meioSomaPG _1 (.a(a1), .b(b1), .p(_1_p), .g(_1_g));
  meioSomaPG _2 (.a(a2), .b(b2), .p(_2_p), .g(_2_g));
  meioSomaPG _3 (.a(a3), .b(b3), .p(_3_p), .g(_3_g));
  xor xor_1 (s0, c0, _0_p);
  or or_1 (s1, _0_g, and_1_out);
  and and_1 (and_1_out, c0, _0_p);
  and and_2 (and_2_out, c0, _0_p, _1_p);
  or or_2 (or_2_out, and_2_out, and_3_out, _1_g);
  and and_3 (and_3_out, _0_g, _1_p);
  and and_4 (and_4_out, c0, _0_p, _1_p, _2_p);
  and and_5 (and_5_out, _0_g, _1_p, _2_p);
  and and_6 (and_6_out, _1_p, _2_p);
  and and_7 (and_7_out, c0, _0_g, _1_p, _2_p, _3_p);
  and and_8 (and_8_out, _0_g, _1_p, _2_p, _3_p);
  and and_9 (and_9_out, _1_g, _2_p, _3_p);
  and and_10 (and_10_out, _2_g, _3_p);
  xor xor_2 (s2, or_2_out, _2_p);
  or or_3 (or_3_out, and_4_out, and_5_out, and_6_out, _2_g);
  xor xor_3 (s3, or_3_out, _3_p);
  or or_4 (c4, and_7_out, and_8_out, and_9_out, and_10_out, _3_g);
endmodule

module CL8bits (
  input  c0,
  input  b0,
  input  a0,
  input  b1,
  input  a1,
  input  b2,
  input  a2,
  input  b3,
  input  a3,
  input  b4,
  input  a4,
  input  b5,
  input  a5,
  input  b6,
  input  a6,
  input  b7,
  input  a7,
  output s0,
  output s1,
  output s2,
  output s3,
  output s4,
  output s5,
  output s6,
  output s7,
  output c8
);

  wire _0_g, _0_p, _1_g, _1_p, _2_g, _2_p, _3_g, _3_p, _4_g, _4_p, _5_g, _5_p, _6_g, _6_p, _7_g, _7_p,
       and_1_out, and_2_out, and_3_out, and_4_out, and_5_out, and_6_out, and_7_out, and_8_out, and_9_out,
       and_10_out, and_11_out, and_12_out, and_13_out, and_14_out, and_15_out, and_16_out, and_17_out,
       and_18_out, and_19_out, and_20_out, and_21_out, and_22_out, and_23_out, and_24_out, and_25_out,
       and_26_out, and_27_out, and_28_out, and_29_out, and_30_out, and_31_out, and_32_out, and_33_out,
       and_34_out, and_35_out, and_36_out, or_2_out, or_3_out, or_4_out, or_5_out, or_6_out, or_7_out;

  meioSomaPG _0 (.a(a0), .b(b0), .p(_0_p), .g(_0_g));
  meioSomaPG _1 (.a(a1), .b(b1), .p(_1_p), .g(_1_g));
  meioSomaPG _2 (.a(a2), .b(b2), .p(_2_p), .g(_2_g));
  meioSomaPG _3 (.a(a3), .b(b3), .p(_3_p), .g(_3_g));
  meioSomaPG _4 (.a(a4), .b(b4), .p(_4_p), .g(_4_g));
  meioSomaPG _6 (.a(a6), .b(b6), .p(_6_p), .g(_6_g));
  meioSomaPG _5 (.a(a5), .b(b5), .p(_5_p), .g(_5_g));
  meioSomaPG _7 (.a(a7), .b(b7), .p(_7_p), .g(_7_g));
  and and_1 (and_1_out, c0, _0_p);
  and and_2 (and_2_out, c0, _0_p, _1_p);
  and and_3 (and_3_out, _0_g, _1_p);
  and and_4 (and_4_out, c0, _0_p, _1_p, _2_p);
  and and_5 (and_5_out, _0_g, _1_p, _2_p);
  and and_6 (and_6_out, _1_g, _2_p);
  and and_7 (and_7_out, c0, _0_p, _1_p, _2_p, _3_p);
  and and_8 (and_8_out, _0_g, _1_p, _2_p, _3_p);
  and and_9 (and_9_out, _1_g, _2_p, _3_p);
  and and_10 (and_10_out, _2_g, _3_p);
  xor xor_1 (s0, c0, _0_p);
  or or_1 (s1, _0_g, and_1_out);
  or or_2 (or_2_out, and_2_out, and_3_out, _1_g);
  or or_3 (or_3_out, and_4_out, and_5_out, and_6_out, _2_g);
  or or_4 (or_4_out, and_7_out, and_8_out, and_9_out, and_10_out, _3_g);
  and and_11 (and_11_out, c0, _0_p, _1_p, _2_p, _3_p, _4_p);
  and and_12 (and_12_out, _0_g, _1_p, _2_p, _3_p, _4_p);
  and and_13 (and_13_out, _1_g, _2_p, _3_p, _4_p);
  and and_14 (and_14_out, _2_g, _3_p, _4_p);
  and and_15 (and_15_out, _3_g, _4_p);
  and and_16 (and_16_out, c0, _0_p, _1_p, _2_p, _3_p, _4_p, _5_p);
  and and_17 (and_17_out, _0_g, _1_p, _2_p, _3_p, _4_p, _5_p);
  and and_18 (and_18_out, _1_g, _2_p, _3_p, _4_p, _5_p);
  and and_19 (and_19_out, _2_g, _3_p, _4_p, _5_p);
  and and_20 (and_20_out, _3_g, _4_p, _5_p);
  and and_21 (and_21_out, _4_g, _5_p);
  and and_22 (and_22_out, c0, _0_p, _1_p, _2_p, _3_p, _4_p, _5_p, _6_p);
  and and_23 (and_23_out, _0_g, _1_p, _2_p, _3_p, _4_p, _5_p, _6_p);
  and and_24 (and_24_out, _1_g, _2_p, _3_p, _4_p, _5_p, _6_p);
  and and_25 (and_25_out, _2_g, _3_p, _4_p, _5_p, _6_p);
  and and_26 (and_26_out, _3_g, _4_p, _5_p, _6_p);
  and and_27 (and_27_out, _4_g, _5_p, _6_p);
  and and_28 (and_28_out, _5_g, _6_p);
  and and_29 (and_29_out, c0, _0_p, _1_p, _2_p, _3_p, _4_p, _5_p, _6_p, _7_p);
  and and_30 (and_30_out, _0_g, _1_p, _2_p, _3_p, _4_p, _5_p, _6_p, _7_p);
  and and_31 (and_31_out, _1_g, _2_p, _3_p, _4_p, _5_p, _6_p, _7_p);
  and and_32 (and_32_out, _2_g, _3_p, _4_p, _5_p, _6_p, _7_p);
  and and_33 (and_33_out, _3_g, _4_p, _5_p, _6_p, _7_p);
  and and_34 (and_34_out, _4_g, _5_p, _6_p, _7_p);
  and and_35 (and_35_out, _5_g, _6_p, _7_p);
  and and_36 (and_36_out, _6_g, _7_p);
  xor xor_2 (s2, or_2_out, _2_p);
  xor xor_3 (s3, or_3_out, _3_p);
  xor xor_4 (s4, or_4_out, _4_p);
  or or_5 (or_5_out, and_11_out, and_12_out, and_13_out, and_14_out, and_15_out, _4_g);
  xor xor_5 (s5, or_5_out, _5_p);
  or or_6 (or_6_out, and_16_out, and_17_out, and_18_out, and_19_out, and_20_out, and_21_out, _5_g);
  or or_7 (or_7_out, and_22_out, and_23_out, and_24_out, and_25_out, and_26_out, and_27_out, and_28_out, _6_g);
  or or_8 (c8, and_29_out, and_30_out, and_31_out, and_32_out, and_33_out, and_34_out, and_35_out, and_36_out, _7_g);
  xor xor_6 (s6, or_6_out, _6_p);
  xor xor_7 (s7, or_7_out, _7_p);
endmodule
