// Logisim project trabalho.circ as structural Verilog
module meioSomaPG (
  input  a,
  input  b,
  output p,
  output g
);

  xor xor_1 (p, b, b);
  and and_1 (g, a, b);
endmodule

module CL4bits (
  input  c0,
  input  b0,
  input  a0,
  input  b1,
  input  a1,
  input  b2,
  input  a2,
  input  b3,
  input  a3,
  output s0,
  output s1,
  output s2,
  output s3,
  output c4
);

  wire _0_g, _0_p, _1_g, _1_p, _2_g, _2_p, _3_g, _3_p, and_1_out, and_2_out, and_3_out, and_4_out, and_5_out,
       and_6_out, and_7_out, and_8_out, and_9_out, and_10_out, or_2_out, or_3_out;

  meioSomaPG _0 (.a(a0), .b(b0), .p(_0_p), .g(_0_g));
  meioSomaPG _1 (.a(a1), .b(b1), .p(_1_p), .g(_1_g));
  meioSomaPG _2 (.a(a2), .b(b2), .p(_2_p), .g(_2_g));
  meioSomaPG _3 (.a(a3), .b(b3), .p(_3_p), .g(_3_g));
  xor xor_1 (s0, c0, _0_p);
  or or_1 (s1, _0_g, and_1_out);
  and and_1 (and_1_out, c0, _0_p);
  and and_2 (and_2_out, c0, _0_p, _1_p);
  or or_2 (or_2_out, and_2_out, and_3_out, _1_g);
  and and_3 (and_3_out, _0_g, _1_p);
  and and_4 (and_4_out, c0, _0_p, _1_p, _2_p);
  and and_5 (and_5_out, _0_g, _1_p, _2_p);
  and and_6 (and_6_out, _1_p, _2_p);
  and and_7 (and_7_out, c0, _0_g, _1_p, _2_p, _3_p);
  and and_8 (and_8_out, _0_g, _1_p, _2_p, _3_p);
  and and_9 (and_9_out, _1_g, _2_p, _3_p);
  and and_10 (and_10_out, _2_g, _3_p);
  xor xor_2 (s2, or_2_out, _2_p);
  or or_3 (or_3_out, and_4_out, and_5_out, and_6_out, _2_g);
  xor xor_3 (s3, or_3_out, _3_p);
  or or_4 (c4, and_7_out, and_8_out, and_9_out, and_10_out, _3_g);
endmodule

module CL8bits (
  input  c0,
  input  b0,
  input  a0,
  input  b1,
  input  a1,
  input  b2,
  input  a2,
  input  b3,
  input  a3,
  input  b4,
  input  a4,
  input  b5,
  input  a5,
  input  b6,
  input  a6,
  input  b7,
  input  a7,
  output s0,
  output s1,
  output s2,
  output s3,
  output c4
);

  wire _0_g, _0_p, _1_g, _1_p, _2_g, _2_p, _3_g, _3_p, _4_g, _4_p, _5_g, _5_p, _6_g, _6_p, _7_g, _7_p,
       and_1_out, and_2_out, and_3_out, and_4_out, and_5_out, and_6_out, and_7_out, and_8_out, and_9_out,
       and_10_out, and_11_out, and_12_out, and_13_out, and_14_out, and_15_out, or_2_out, or_3_out;

  meioSomaPG _0 (.a(a0), .b(b0), .p(_0_p), .g(_0_g));
  meioSomaPG _1 (.a(a1), .b(b1), .p(_1_p), .g(_1_g));
  meioSomaPG _2 (.a(a2), .b(b2), .p(_2_p), .g(_2_g));
  meioSomaPG _3 (.a(a3), .b(b3), .p(_3_p), .g(_3_g));
  meioSomaPG _4 (.a(a4), .b(b4), .p(_4_p), .g(_4_g));
  meioSomaPG _6 (.a(a6), .b(b6), .p(_6_p), .g(_6_g));
  meioSomaPG _5 (.a(a5), .b(b5), .p(_5_p), .g(_5_g));
  meioSomaPG _7 (.a(a7), .b(b7), .p(_7_p), .g(_7_g));
  and and_1 (and_1_out, c0, _0_p);
  and and_2 (and_2_out, c0, _0_p, _1_p);
  and and_3 (and_3_out, _0_g, _1_p);
  and and_4 (and_4_out, c0, _0_p, _1_p, _2_p);
  and and_5 (and_5_out, _0_g, _1_p, _2_p);
  and and_6 (and_6_out, _1_p, _2_p);
  and and_7 (and_7_out, c0, _0_g, _1_p, _2_p, _3_p);
  and and_8 (and_8_out, _0_g, _1_p, _2_p, _3_p);
  and and_9 (and_9_out, _1_g, _2_p, _3_p);
  and and_10 (and_10_out, _2_g, _3_p);
  xor xor_1 (s0, c0, _0_p);
  or or_1 (s1, _0_g, and_1_out);
  or or_2 (or_2_out, and_2_out, and_3_out, _1_g);
  or or_3 (or_3_out, and_4_out, and_5_out, and_6_out, _2_g);
  or or_4 (c4, and_7_out, and_8_out, and_9_out, and_10_out, _3_g);
  and and_11 (and_11_out, c0, _0_p, _1_p, _2_p, _3_p, _4_p);
  and and_12 (and_12_out, _0_g, _1_p, _2_p, _3_p, _4_p);
  and and_13 (and_13_out, _1_g, _2_p, _3_p, _4_p);
  and and_14 (and_14_out, _2_g, _3_p, _4_p);
  and and_15 (and_15_out, _3_g, _4_p);
  // AND_Gate and_16 has open pins: in0=c0, in1=_0_p, in2=_1_p, in3=_2_p, in4=_3_p, in5=_4_p, in6=_5_p, out=open
  // AND_Gate and_17 has open pins: in0=_0_g, in1=_1_p, in2=_2_p, in3=_3_p, in4=_4_p, in5=_5_p, out=open
  // AND_Gate and_18 has open pins: in0=_1_g, in1=_2_p, in2=_3_p, in3=_4_p, in4=_5_p, out=open
  // AND_Gate and_19 has open pins: in0=_2_g, in1=_3_p, in2=_4_p, in3=_5_p, out=open
  // AND_Gate and_20 is placed but not wired
  // AND_Gate and_21 is placed but not wired
  xor xor_2 (s2, or_2_out, _2_p);
  xor xor_3 (s3, or_3_out, _3_p);
  // OR_Gate or_5 has open pins: in0=and_11_out, in1=and_12_out, in2=and_13_out, in3=and_14_out, in4=and_15_out, in5=_4_g, out=open
  // OR_Gate or_6 is placed but not wired
endmodule
